// Logisim project CRC.circ as structural Verilog: 2 circuits, main circuit CRC
module CRC (
  input  [7:0] in_1,
  input  [3:0] in_2,
  output [10:0] out_3
);

  wire [2:0] crc_1_1_out_3, crc_1_2_out_3, crc_1_3_out_3, crc_1_4_out_3, crc_1_5_out_3, crc_1_6_out_3,
       crc_1_7_out_3;

  CRC_1 crc_1_1 (.\被除数 (in_1[7:4]), .\除数 (in_2), .out_3(crc_1_1_out_3));  // open: out_4
  CRC_1 crc_1_2 (.\被除数 ({crc_1_1_out_3, in_1[3]}), .\除数 (in_2), .out_3(crc_1_2_out_3));  // open: out_4
  CRC_1 crc_1_3 (.\被除数 ({crc_1_2_out_3, in_1[2]}), .\除数 (in_2), .out_3(crc_1_3_out_3));  // open: out_4
  CRC_1 crc_1_4 (.\被除数 ({crc_1_3_out_3, in_1[1]}), .\除数 (in_2), .out_3(crc_1_4_out_3));  // open: out_4
  CRC_1 crc_1_5 (.\被除数 ({crc_1_4_out_3, in_1[0]}), .\除数 (in_2), .out_3(crc_1_5_out_3));  // open: out_4
  CRC_1 crc_1_6 (.\被除数 ({crc_1_5_out_3, 1'b0}), .\除数 (in_2), .out_3(crc_1_6_out_3));  // open: out_4
  CRC_1 crc_1_7 (.\被除数 ({crc_1_6_out_3, 1'b0}), .\除数 (in_2), .out_3(crc_1_7_out_3));  // open: out_4
  CRC_1 crc_1_8 (.\被除数 ({crc_1_7_out_3, 1'b0}), .\除数 (in_2), .out_3(out_3[2:0]));  // open: out_4

  assign out_3[10:3] = in_1;

  // Other names for the same wires on the sheet: o0 = out_3[0]; o1 = out_3[1]; o2 = out_3[2]
endmodule

module CRC_1 (
  input  [3:0] \被除数 ,
  input  [3:0] \除数 ,
  output [2:0] out_3,
  output out_4
);

  wire [3:0] xor_1_out;

  assign xor_1_out = \被除数  ^ \除数 ;  // XOR_Gate xor_1, 4 bits wide
  Multiplexer #(.width(3)) multiplexer_1 (
    .in0(\被除数 [2:0]), .in1(xor_1_out[2:0]), .out(out_3), .sel(\被除数 [3]));  // open: en

  assign out_4 = \被除数 [3];

  // Other names for the same wires on the sheet: if = \被除数 [3]
endmodule
