// Logisim project fsm.circ as structural Verilog: 2 circuits, main circuit fsm
module fsm (
  input  in_1,
  input  [1:0] In,
  output out_3
);

  wire clock_1_out;
  wire [2:0] multiplexer_1_out, register_1_q, status_1__s2;

  status status_1 (
    .S2(register_1_q[0]), ._S2(status_1__s2[0]), .S1(register_1_q[1]), .S0(register_1_q[2]), .In1(In[1]),
    .In0(In[0]), ._S1(status_1__s2[1]), ._S0(status_1__s2[2]), .Z(out_3));
  Multiplexer #(.width(3)) multiplexer_1 (
    .in0(status_1__s2), .in1(3'b000), .out(multiplexer_1_out), .sel(in_1));  // open: en
  Register #(.width(3)) register_1 (.D(multiplexer_1_out), .Q(register_1_q), .clk(clock_1_out));  // open: en, clr
  Clock clock_1 (.out(clock_1_out));
endmodule

module status (
  input  S2,
  input  S1,
  input  S0,
  input  In1,
  input  In0,
  output _S2,
  output _S1,
  output _S0,
  output Z
);

  wire and_1_out, and_2_out, and_3_out, and_4_out, and_5_out, and_6_out, and_7_out, and_8_out, and_9_out,
       and_10_out, and_11_out, and_12_out, and_13_out, not_1_out, not_2_out, not_3_out, not_4_out, not_5_out,
       not_6_out, not_7_out, not_8_out, not_9_out, not_10_out, not_11_out, not_12_out, not_13_out,
       not_14_out, not_15_out, not_16_out, not_17_out, not_18_out, not_19_out, not_20_out, not_21_out,
       not_22_out;

  not not_1 (not_1_out, In0);
  not not_2 (not_2_out, In1);
  not not_3 (not_3_out, In0);
  not not_4 (not_4_out, S1);
  not not_5 (not_5_out, In1);
  not not_6 (not_6_out, S1);
  not not_7 (not_7_out, In0);
  not not_8 (not_8_out, S0);
  not not_9 (not_9_out, In1);
  not not_10 (not_10_out, S0);
  not not_11 (not_11_out, In0);
  not not_12 (not_12_out, S1);
  not not_13 (not_13_out, S0);
  not not_14 (not_14_out, In1);
  not not_15 (not_15_out, S1);
  not not_16 (not_16_out, In0);
  not not_17 (not_17_out, S0);
  not not_18 (not_18_out, In0);
  not not_19 (not_19_out, In1);
  not not_20 (not_20_out, In0);
  not not_21 (not_21_out, In0);
  not not_22 (not_22_out, In0);
  and and_1 (and_1_out, S1, S0, not_1_out);
  and and_2 (and_2_out, S2, S0, not_2_out, not_3_out);
  and and_3 (and_3_out, not_4_out, S0, not_5_out);
  and and_4 (and_4_out, not_6_out, S0, not_7_out);
  and and_5 (and_5_out, S1, not_8_out, not_9_out);
  and and_6 (and_6_out, S1, not_10_out, not_11_out);
  and and_7 (and_7_out, not_12_out, not_13_out, not_14_out, In0);
  and and_8 (and_8_out, not_15_out, S0, not_16_out);
  and and_9 (and_9_out, S1, not_17_out, not_18_out);
  and and_10 (and_10_out, S1, S0, not_19_out, In0);
  and and_11 (and_11_out, S1, S0, not_20_out);
  and and_12 (and_12_out, S2, S0, not_21_out);
  and and_13 (and_13_out, S2, S1, not_22_out);
  or or_1 (_S2, and_1_out, and_2_out);
  or or_2 (_S1, and_3_out, and_4_out, and_5_out, and_6_out);
  or or_3 (_S0, and_7_out, and_8_out, and_9_out, and_10_out);
  or or_4 (Z, and_11_out, and_12_out, and_13_out);
endmodule
