// Logisim project grf.circ as structural Verilog: 1 circuit, main circuit grf
module grf (
  input  in_1,
  input  in_2,
  input  in_3,
  input  [31:0] WD,
  input  [4:0] A3,
  input  [4:0] A1,
  input  [4:0] A2,
  output [31:0] RD1,
  output [31:0] RD2
);

  wire we0, we1, we2, we3, we4, we5, we6, we7, we8, we9, we10, we11, we12, we13, we14, we15, we16, we17,
       we18, we19, we20, we21, we22, we23, we24, we25, we26, we27, we28, we29, we30, we31;
  wire [31:0] in0, in1, in2, in3, in4, in5, in6, in7, in8, in9, in10, in11, in12, in13, in14, in15, in16,
       in17, in18, in19, in20, in21, in22, in23, in24, in25, in26, in27, in28, in29, in30, in31, out0, out1,
       out2, out3, out4, out5, out6, out7, out8, out9, out10, out11, out12, out13, out14, out15, out16,
       out17, out18, out19, out20, out21, out22, out23, out24, out25, out26, out27, out28, out29, out30,
       out31;

  Demultiplexer #(.select(5), .width(32)) demultiplexer_1 (
    .out0(in0), .out1(in1), .out2(in2), .out3(in3), .out4(in4), .out5(in5), .out6(in6), .out7(in7),
    .out8(in8), .out9(in9), .out10(in10), .out11(in11), .out12(in12), .out13(in13), .out14(in14),
    .out15(in15), .out16(in16), .out17(in17), .out18(in18), .out19(in19), .out20(in20), .out21(in21),
    .out22(in22), .out23(in23), .out24(in24), .out25(in25), .out26(in26), .out27(in27), .out28(in28),
    .out29(in29), .out30(in30), .out31(in31), .in(WD), .sel(A3));  // open: en
  Demultiplexer #(.select(5)) demultiplexer_2 (
    .out0(we0), .out1(we1), .out2(we2), .out3(we3), .out4(we4), .out5(we5), .out6(we6), .out7(we7),
    .out8(we8), .out9(we9), .out10(we10), .out11(we11), .out12(we12), .out13(we13), .out14(we14),
    .out15(we15), .out16(we16), .out17(we17), .out18(we18), .out19(we19), .out20(we20), .out21(we21),
    .out22(we22), .out23(we23), .out24(we24), .out25(we25), .out26(we26), .out27(we27), .out28(we28),
    .out29(we29), .out30(we30), .out31(we31), .in(in_3), .sel(A3));  // open: en
  Register #(.width(32)) register_1 (.D(in0), .en(we0), .Q(out0), .clk(in_1), .clr(in_2));
  Register #(.width(32)) register_2 (.D(in1), .en(we1), .Q(out1), .clk(in_1), .clr(in_2));
  Register #(.width(32)) register_3 (.D(in2), .en(we2), .Q(out2), .clk(in_1), .clr(in_2));
  Register #(.width(32)) register_4 (.D(in3), .en(we3), .Q(out3), .clk(in_1), .clr(in_2));
  Register #(.width(32)) register_5 (.D(in4), .en(we4), .Q(out4), .clk(in_1), .clr(in_2));
  Register #(.width(32)) register_6 (.D(in5), .en(we5), .Q(out5), .clk(in_1), .clr(in_2));
  Register #(.width(32)) register_7 (.D(in6), .en(we6), .Q(out6), .clk(in_1), .clr(in_2));
  Register #(.width(32)) register_8 (.D(in7), .en(we7), .Q(out7), .clk(in_1), .clr(in_2));
  Register #(.width(32)) register_9 (.D(in8), .en(we8), .Q(out8), .clk(in_1), .clr(in_2));
  Register #(.width(32)) register_10 (.D(in9), .en(we9), .Q(out9), .clk(in_1), .clr(in_2));
  Register #(.width(32)) register_11 (.D(in10), .en(we10), .Q(out10), .clk(in_1), .clr(in_2));
  Register #(.width(32)) register_12 (.D(in11), .en(we11), .Q(out11), .clk(in_1), .clr(in_2));
  Register #(.width(32)) register_13 (.D(in12), .en(we12), .Q(out12), .clk(in_1), .clr(in_2));
  Register #(.width(32)) register_14 (.D(in13), .en(we13), .Q(out13), .clk(in_1), .clr(in_2));
  Register #(.width(32)) register_15 (.D(in14), .en(we14), .Q(out14), .clk(in_1), .clr(in_2));
  Register #(.width(32)) register_16 (.D(in15), .en(we15), .Q(out15), .clk(in_1), .clr(in_2));
  Register #(.width(32)) register_17 (.D(in16), .en(we16), .Q(out16), .clk(in_1), .clr(in_2));
  Register #(.width(32)) register_18 (.D(in17), .en(we17), .Q(out17), .clk(in_1), .clr(in_2));
  Register #(.width(32)) register_19 (.D(in18), .en(we18), .Q(out18), .clk(in_1), .clr(in_2));
  Register #(.width(32)) register_20 (.D(in19), .en(we19), .Q(out19), .clk(in_1), .clr(in_2));
  Register #(.width(32)) register_21 (.D(in20), .en(we20), .Q(out20), .clk(in_1), .clr(in_2));
  Register #(.width(32)) register_22 (.D(in21), .en(we21), .Q(out21), .clk(in_1), .clr(in_2));
  Register #(.width(32)) register_23 (.D(in22), .en(we22), .Q(out22), .clk(in_1), .clr(in_2));
  Register #(.width(32)) register_24 (.D(in23), .en(we23), .Q(out23), .clk(in_1), .clr(in_2));
  Register #(.width(32)) register_25 (.D(in24), .en(we24), .Q(out24), .clk(in_1), .clr(in_2));
  Register #(.width(32)) register_26 (.D(in25), .en(we25), .Q(out25), .clk(in_1), .clr(in_2));
  Register #(.width(32)) register_27 (.D(in26), .en(we26), .Q(out26), .clk(in_1), .clr(in_2));
  Register #(.width(32)) register_28 (.D(in27), .en(we27), .Q(out27), .clk(in_1), .clr(in_2));
  Register #(.width(32)) register_29 (.D(in28), .en(we28), .Q(out28), .clk(in_1), .clr(in_2));
  Register #(.width(32)) register_30 (.D(in29), .en(we29), .Q(out29), .clk(in_1), .clr(in_2));
  Register #(.width(32)) register_31 (.D(in30), .en(we30), .Q(out30), .clk(in_1), .clr(in_2));
  Register #(.width(32)) register_32 (.D(in31), .en(we31), .Q(out31), .clk(in_1), .clr(in_2));
  Multiplexer #(.select(5), .width(32)) multiplexer_1 (
    .in0({32{1'b0}}), .in1(out1), .in2(out2), .in3(out3), .in4(out4), .in5(out5), .in6(out6), .in7(out7),
    .in8(out8), .in9(out9), .in10(out10), .in11(out11), .in12(out12), .in13(out13), .in14(out14),
    .in15(out15), .in16(out16), .in17(out17), .in18(out18), .in19(out19), .in20(out20), .in21(out21),
    .in22(out22), .in23(out23), .in24(out24), .in25(out25), .in26(out26), .in27(out27), .in28(out28),
    .in29(out29), .in30(out30), .in31(out31), .out(RD1), .sel(A1));  // open: en
  Multiplexer #(.select(5), .width(32)) multiplexer_2 (
    .in0({32{1'b0}}), .in1(out1), .in2(out2), .in3(out3), .in4(out4), .in5(out5), .in6(out6), .in7(out7),
    .in8(out8), .in9(out9), .in10(out10), .in11(out11), .in12(out12), .in13(out13), .in14(out14),
    .in15(out15), .in16(out16), .in17(out17), .in18(out18), .in19(out19), .in20(out20), .in21(out21),
    .in22(out22), .in23(out23), .in24(out24), .in25(out25), .in26(out26), .in27(out27), .in28(out28),
    .in29(out29), .in30(out30), .in31(out31), .out(RD2), .sel(A2));  // open: en

  // Other names for the same wires on the sheet: clk = in_1; reset = in_2
endmodule
