// Logisim project navigation.circ as structural Verilog: 2 circuits, main circuit navigation
module navigation (
  input  [1:0] in_1,
  input  in_2,
  input  in_3,
  output hit,
  output arrive
);

  wire status_1_arrive, status_1_hit;
  wire [2:0] register_1_q, status_1__s0;

  status status_1 (
    .S2(register_1_q[2]), .S1(register_1_q[1]), .S0(register_1_q[0]), .dir0(in_1[1]), .dir1(in_1[0]),
    ._S2(status_1__s0[2]), ._S1(status_1__s0[1]), ._S0(status_1__s0[0]), .hit(status_1_hit),
    .arrive(status_1_arrive));
  Register #(.width(3)) register_1 (.D(status_1__s0), .Q(register_1_q), .clk(in_2), .clr(in_3));  // open: en
  Register #(.width(1)) register_2 (.D(status_1_hit), .Q(hit), .clk(in_2), .clr(in_3));  // open: en
  Register #(.width(1)) register_3 (.D(status_1_arrive), .Q(arrive), .clk(in_2), .clr(in_3));  // open: en
endmodule

module status (
  input  S2,
  input  S1,
  input  S0,
  input  dir0,
  input  dir1,
  output _S2,
  output _S1,
  output _S0,
  output hit,
  output arrive
);

  wire and_1_out, and_2_out, and_3_out, and_4_out, and_5_out, and_6_out, and_7_out, and_8_out, and_9_out,
       and_10_out, and_11_out, and_12_out, and_13_out, and_14_out, and_15_out, and_16_out, and_17_out,
       and_18_out, not_1_out, not_2_out, not_3_out, not_4_out, not_5_out, not_6_out, not_7_out, not_8_out,
       not_9_out, not_10_out, not_11_out, not_12_out, not_13_out, not_14_out, not_15_out, not_16_out,
       not_17_out, not_18_out, not_19_out, not_20_out, not_21_out, not_22_out, not_23_out, not_24_out,
       not_25_out, not_26_out, not_27_out, not_28_out, not_29_out, not_30_out, not_31_out, not_32_out,
       not_33_out, not_34_out;

  not not_1 (not_1_out, S0);
  not not_2 (not_2_out, dir0);
  not not_3 (not_3_out, dir1);
  not not_4 (not_4_out, dir0);
  not not_5 (not_5_out, S2);
  not not_6 (not_6_out, S1);
  not not_7 (not_7_out, dir0);
  not not_8 (not_8_out, S2);
  not not_9 (not_9_out, dir0);
  not not_10 (not_10_out, dir1);
  not not_11 (not_11_out, S0);
  not not_12 (not_12_out, dir0);
  not not_13 (not_13_out, S0);
  not not_14 (not_14_out, dir1);
  not not_15 (not_15_out, S2);
  not not_16 (not_16_out, S1);
  not not_17 (not_17_out, dir0);
  not not_18 (not_18_out, dir1);
  not not_19 (not_19_out, dir1);
  not not_20 (not_20_out, S2);
  not not_21 (not_21_out, S0);
  not not_22 (not_22_out, dir0);
  not not_23 (not_23_out, S2);
  not not_24 (not_24_out, S1);
  not not_25 (not_25_out, S0);
  not not_26 (not_26_out, S2);
  not not_27 (not_27_out, S0);
  not not_28 (not_28_out, dir1);
  not not_29 (not_29_out, dir0);
  not not_30 (not_30_out, dir1);
  not not_31 (not_31_out, S0);
  not not_32 (not_32_out, dir0);
  not not_33 (not_33_out, dir1);
  not not_34 (not_34_out, dir0);
  and and_1 (and_1_out, S1, not_1_out, not_2_out, not_3_out);
  and and_2 (and_2_out, S1, S0, not_4_out, dir1);
  and and_3 (and_3_out, not_5_out, not_6_out, S0, not_7_out);
  and and_4 (and_4_out, not_8_out, S0, not_9_out, not_10_out);
  and and_5 (and_5_out, S1, not_11_out, not_12_out, dir1);
  and and_6 (and_6_out, S1, not_13_out, dir0, not_14_out);
  and and_7 (and_7_out, S1, S0, dir0, dir1);
  and and_8 (and_8_out, not_15_out, not_16_out, not_17_out, not_18_out);
  and and_9 (and_9_out, S0, dir0, dir1);
  and and_10 (and_10_out, S1, dir0, dir1);
  and and_11 (and_11_out, S1, S0, not_19_out);
  and and_12 (and_12_out, not_20_out, not_21_out, not_22_out, dir1);
  and and_13 (and_13_out, not_23_out, not_24_out, not_25_out, dir0);
  and and_14 (and_14_out, not_26_out, not_27_out, dir0, not_28_out);
  and and_15 (and_15_out, S0, dir0, dir1);
  and and_16 (and_16_out, S1, S0, not_29_out, not_30_out);
  and and_17 (and_17_out, S1, not_31_out, not_32_out, not_33_out);
  and and_18 (and_18_out, S1, S0, not_34_out, dir1);
  or or_1 (_S2, and_1_out, and_2_out);
  or or_2 (_S1, and_3_out, and_4_out, and_5_out, and_6_out, and_7_out);
  or or_3 (_S0, and_8_out, and_9_out, and_10_out, and_11_out);
  or or_4 (hit, and_12_out, and_13_out, and_14_out, and_15_out, and_16_out);
  or or_5 (arrive, and_17_out, and_18_out);
endmodule
