// Logisim project test.circ as structural Verilog: 12 circuits, main circuit main
module main (
  input  reset,
  output [31:0] out_2,
  output out_3,
  output [4:0] out_4,
  output [31:0] out_5,
  output out_6,
  output [4:0] out_7,
  output [31:0] out_8
);

  wire ALUSrc, clk, controller_1_branch, extsel, MemRead, MemtoReg, PCSrc, RegDst, zero;
  wire [3:0] ALUCtrl;
  wire [31:0] alu_1_out_5, ext_1_out_3, grf_1_rd1, multiplexer_2_out, ram_1_data;

  Clock clock_1 (.out(clk));
  Multiplexer #(.width(5)) multiplexer_1 (
    .in0(out_2[20:16]), .in1(out_2[15:11]), .out(out_4), .sel(RegDst));  // open: en
  EXT ext_1 (.in_1(out_2[15:0]), .out_3(ext_1_out_3), .extsel(extsel));
  grf grf_1 (
    .WD(out_5), .RD1(grf_1_rd1), .RD2(out_8), .clk(clk), .reset(reset), .we(out_3), .A3(out_4),
    .A1(out_2[25:21]), .A2(out_2[20:16]));
  IFU ifu_1 (
    .clk(clk), .reset(reset), .out_7(out_2), ._26bits(out_2[25:0]), .PCSrc(PCSrc), .PCJump(MemRead),
    .in_4(out_2[15:0]));
  Multiplexer #(.width(32)) multiplexer_2 (
    .in0(out_8), .in1(ext_1_out_3), .out(multiplexer_2_out), .sel(ALUSrc));  // open: en
  ALU alu_1 (.in1(grf_1_rd1), .in2(multiplexer_2_out), .OP(ALUCtrl), .out_5(alu_1_out_5), .zero(zero));
  sel26 sel26_1 (.in_1(alu_1_out_5), .out_2(out_7));
  Controller controller_1 (
    .RegDst(RegDst), .RegWrite(out_3), .ALUSrc(ALUSrc), .branch(controller_1_branch), .PCJump(MemRead),
    .MemRead(MemRead), .MemWrite(out_6), .MemtoReg(MemtoReg), .ALU(ALUCtrl), .op(out_2[31:26]),
    .func(out_2[5:0]), .extsel(extsel));
  RAM #(.addrWidth(5), .dataWidth(32), .bus("separate")) ram_1 (
    .addr(out_7), .din(out_8), .data(ram_1_data), .str(out_6), .clk(clk), .ld(MemRead), .clr(reset));  // open: sel
  Multiplexer #(.width(32)) multiplexer_3 (
    .in0(alu_1_out_5), .in1(ram_1_data), .out(out_5), .sel(MemtoReg));  // open: en
  and and_1 (PCSrc, zero, controller_1_branch);
  // Probe on out_2

  // Other names for the same wires on the sheet: _26bits[25:0] = out_2[25:0]; func[5:0] = out_2[5:0];
  //   imm16[15:0] = out_2[15:0]; Instr[31:0] = out_2; rd[4:0] = out_2[15:11]; rt[4:0] = out_2[20:16];
  //   rs[4:0] = out_2[25:21]; op[5:0] = out_2[31:26]; MemAddr[4:0] = out_7; MemData[31:0] = out_8; MemWrite = out_6;
  //   PCJump = MemRead; RegAddr[4:0] = out_4; RegData[31:0] = out_5; RegWrite = out_3
endmodule

module ALU (
  input  [31:0] in1,
  input  [31:0] in2,
  input  [3:0] OP,
  output zero,
  output [31:0] out_5
);

  wire [31:0] add_1_out_3, and_1_out_3, or_1_out_3, shifter_1_out, sub_1_out_3;

  add add_1 (.in_1(in1), .in_2(in2), .out_3(add_1_out_3));
  sub sub_1 (.in_1(in1), .in_2(in2), .out_3(sub_1_out_3));
  \or  or_1 (.in_1(in1), .in_2(in2), .out_3(or_1_out_3));
  \and  and_1 (.in_1(in1), .in_2(in2), .out_3(and_1_out_3));
  Shifter #(.width(32)) shifter_1 (.in(in2), .\dist (5'b10000), .out(shifter_1_out));
  Multiplexer #(.select(4), .width(32)) multiplexer_1 (
    .in0(add_1_out_3), .in1(sub_1_out_3), .in2(or_1_out_3), .in3(and_1_out_3), .in4(shifter_1_out),
    .out(out_5), .sel(OP));  // open: in5, in6, in7, in8, in9, in10, in11, in12, in13, in14, in15, en
  Comparator #(.width(32), .mode("unsigned")) comparator_1 (.a(out_5), .b({32{1'b0}}), .eq(zero));  // open: gt, lt
endmodule

module add (
  input  [31:0] in_1,
  input  [31:0] in_2,
  output [31:0] out_3
);

  Adder #(.width(32)) adder_1 (.a(in_1), .b(in_2), .out(out_3));  // open: cin, cout
endmodule

module sub (
  input  [31:0] in_1,
  input  [31:0] in_2,
  output [31:0] out_3
);

  Subtractor #(.width(32)) subtractor_1 (.a(in_1), .b(in_2), .out(out_3));  // open: bin, bout
endmodule

module \or  (
  input  [31:0] in_1,
  input  [31:0] in_2,
  output [31:0] out_3
);

  assign out_3 = in_1 | in_2;  // OR_Gate or_1, 32 bits wide
endmodule

module grf (
  input  clk,
  input  reset,
  input  we,
  input  [31:0] WD,
  input  [4:0] A3,
  input  [4:0] A1,
  input  [4:0] A2,
  output [31:0] RD1,
  output [31:0] RD2
);

  wire we0, we1, we2, we3, we4, we5, we6, we7, we8, we9, we10, we11, we12, we13, we14, we15, we16, we17,
       we18, we19, we20, we21, we22, we23, we24, we25, we26, we27, we28, we29, we30, we31;
  wire [31:0] in0, in1, in2, in3, in4, in5, in6, in7, in8, in9, in10, in11, in12, in13, in14, in15, in16,
       in17, in18, in19, in20, in21, in22, in23, in24, in25, in26, in27, in28, in29, in30, in31, out0, out1,
       out2, out3, out4, out5, out6, out7, out8, out9, out10, out11, out12, out13, out14, out15, out16,
       out17, out18, out19, out20, out21, out22, out23, out24, out25, out26, out27, out28, out29, out30,
       out31;

  Demultiplexer #(.select(5), .width(32)) demultiplexer_1 (
    .out0(in0), .out1(in1), .out2(in2), .out3(in3), .out4(in4), .out5(in5), .out6(in6), .out7(in7),
    .out8(in8), .out9(in9), .out10(in10), .out11(in11), .out12(in12), .out13(in13), .out14(in14),
    .out15(in15), .out16(in16), .out17(in17), .out18(in18), .out19(in19), .out20(in20), .out21(in21),
    .out22(in22), .out23(in23), .out24(in24), .out25(in25), .out26(in26), .out27(in27), .out28(in28),
    .out29(in29), .out30(in30), .out31(in31), .in(WD), .sel(A3));  // open: en
  Demultiplexer #(.select(5)) demultiplexer_2 (
    .out0(we0), .out1(we1), .out2(we2), .out3(we3), .out4(we4), .out5(we5), .out6(we6), .out7(we7),
    .out8(we8), .out9(we9), .out10(we10), .out11(we11), .out12(we12), .out13(we13), .out14(we14),
    .out15(we15), .out16(we16), .out17(we17), .out18(we18), .out19(we19), .out20(we20), .out21(we21),
    .out22(we22), .out23(we23), .out24(we24), .out25(we25), .out26(we26), .out27(we27), .out28(we28),
    .out29(we29), .out30(we30), .out31(we31), .in(we), .sel(A3));  // open: en
  Register #(.width(32)) register_1 (.D({32{1'b0}}), .en(we0), .Q(out0), .clk(clk), .clr(reset));
  Register #(.width(32)) register_2 (.D(in1), .en(we1), .Q(out1), .clk(clk), .clr(reset));
  Register #(.width(32)) register_3 (.D(in2), .en(we2), .Q(out2), .clk(clk), .clr(reset));
  Register #(.width(32)) register_4 (.D(in3), .en(we3), .Q(out3), .clk(clk), .clr(reset));
  Register #(.width(32)) register_5 (.D(in4), .en(we4), .Q(out4), .clk(clk), .clr(reset));
  Register #(.width(32)) register_6 (.D(in5), .en(we5), .Q(out5), .clk(clk), .clr(reset));
  Register #(.width(32)) register_7 (.D(in6), .en(we6), .Q(out6), .clk(clk), .clr(reset));
  Register #(.width(32)) register_8 (.D(in7), .en(we7), .Q(out7), .clk(clk), .clr(reset));
  Register #(.width(32)) register_9 (.D(in8), .en(we8), .Q(out8), .clk(clk), .clr(reset));
  Register #(.width(32)) register_10 (.D(in9), .en(we9), .Q(out9), .clk(clk), .clr(reset));
  Register #(.width(32)) register_11 (.D(in10), .en(we10), .Q(out10), .clk(clk), .clr(reset));
  Register #(.width(32)) register_12 (.D(in11), .en(we11), .Q(out11), .clk(clk), .clr(reset));
  Register #(.width(32)) register_13 (.D(in12), .en(we12), .Q(out12), .clk(clk), .clr(reset));
  Register #(.width(32)) register_14 (.D(in13), .en(we13), .Q(out13), .clk(clk), .clr(reset));
  Register #(.width(32)) register_15 (.D(in14), .en(we14), .Q(out14), .clk(clk), .clr(reset));
  Register #(.width(32)) register_16 (.D(in15), .en(we15), .Q(out15), .clk(clk), .clr(reset));
  Register #(.width(32)) register_17 (.D(in16), .en(we16), .Q(out16), .clk(clk), .clr(reset));
  Register #(.width(32)) register_18 (.D(in17), .en(we17), .Q(out17), .clk(clk), .clr(reset));
  Register #(.width(32)) register_19 (.D(in18), .en(we18), .Q(out18), .clk(clk), .clr(reset));
  Register #(.width(32)) register_20 (.D(in19), .en(we19), .Q(out19), .clk(clk), .clr(reset));
  Register #(.width(32)) register_21 (.D(in20), .en(we20), .Q(out20), .clk(clk), .clr(reset));
  Register #(.width(32)) register_22 (.D(in21), .en(we21), .Q(out21), .clk(clk), .clr(reset));
  Register #(.width(32)) register_23 (.D(in22), .en(we22), .Q(out22), .clk(clk), .clr(reset));
  Register #(.width(32)) register_24 (.D(in23), .en(we23), .Q(out23), .clk(clk), .clr(reset));
  Register #(.width(32)) register_25 (.D(in24), .en(we24), .Q(out24), .clk(clk), .clr(reset));
  Register #(.width(32)) register_26 (.D(in25), .en(we25), .Q(out25), .clk(clk), .clr(reset));
  Register #(.width(32)) register_27 (.D(in26), .en(we26), .Q(out26), .clk(clk), .clr(reset));
  Register #(.width(32)) register_28 (.D(in27), .en(we27), .Q(out27), .clk(clk), .clr(reset));
  Register #(.width(32)) register_29 (.D(in28), .en(we28), .Q(out28), .clk(clk), .clr(reset));
  Register #(.width(32)) register_30 (.D(in29), .en(we29), .Q(out29), .clk(clk), .clr(reset));
  Register #(.width(32)) register_31 (.D(in30), .en(we30), .Q(out30), .clk(clk), .clr(reset));
  Register #(.width(32)) register_32 (.D(in31), .en(we31), .Q(out31), .clk(clk), .clr(reset));
  Multiplexer #(.select(5), .width(32)) multiplexer_1 (
    .in0({32{1'b0}}), .in1(out1), .in2(out2), .in3(out3), .in4(out4), .in5(out5), .in6(out6), .in7(out7),
    .in8(out8), .in9(out9), .in10(out10), .in11(out11), .in12(out12), .in13(out13), .in14(out14),
    .in15(out15), .in16(out16), .in17(out17), .in18(out18), .in19(out19), .in20(out20), .in21(out21),
    .in22(out22), .in23(out23), .in24(out24), .in25(out25), .in26(out26), .in27(out27), .in28(out28),
    .in29(out29), .in30(out30), .in31(out31), .out(RD1), .sel(A1));  // open: en
  Multiplexer #(.select(5), .width(32)) multiplexer_2 (
    .in0({32{1'b0}}), .in1(out1), .in2(out2), .in3(out3), .in4(out4), .in5(out5), .in6(out6), .in7(out7),
    .in8(out8), .in9(out9), .in10(out10), .in11(out11), .in12(out12), .in13(out13), .in14(out14),
    .in15(out15), .in16(out16), .in17(out17), .in18(out18), .in19(out19), .in20(out20), .in21(out21),
    .in22(out22), .in23(out23), .in24(out24), .in25(out25), .in26(out26), .in27(out27), .in28(out28),
    .in29(out29), .in30(out30), .in31(out31), .out(RD2), .sel(A2));  // open: en
endmodule

module PC_add (
  input  [31:0] in_1,
  output [31:0] out_2
);

  Adder #(.width(32)) adder_1 (.a(in_1), .b(32'h4), .out(out_2));  // open: cin, cout
endmodule

module IFU (
  input  [25:0] _26bits,
  input  PCSrc,
  input  PCJump,
  input  [15:0] in_4,
  input  clk,
  input  reset,
  output [31:0] out_7
);

  wire [3:0] pc_add_1_out_2;
  wire [4:0] sel26_1_out_2;
  wire [17:0] bit_extender_2_out, shifter_2_out;
  wire [27:0] bit_extender_1_out, pc_add_1_out_2_2, shifter_1_out;
  wire [31:0] adder_1_out, bit_extender_3_out, multiplexer_1_out, multiplexer_2_out, PC_q;

  Register #(.width(32)) PC (.D(multiplexer_2_out), .Q(PC_q), .clk(clk), .clr(reset));  // open: en
  assign bit_extender_1_out = {{2{1'b0}}, _26bits};  // Bit_Extender bit_extender_1
  Shifter #(.width(28)) shifter_1 (.in(bit_extender_1_out), .\dist (5'b00010), .out(shifter_1_out));
  PC_add pc_add_1 (.in_1(PC_q), .out_2({pc_add_1_out_2, pc_add_1_out_2_2}));
  sel26 sel26_1 (.in_1(PC_q), .out_2(sel26_1_out_2));
  assign bit_extender_2_out = {{2{1'b0}}, in_4};  // Bit_Extender bit_extender_2
  Shifter #(.width(18)) shifter_2 (.in(bit_extender_2_out), .\dist (5'b00010), .out(shifter_2_out));
  ROM #(.addrWidth(5), .dataWidth(32)) rom_1 (.addr(sel26_1_out_2), .data(out_7));  // open: sel
  assign bit_extender_3_out = {{14{1'b0}}, shifter_2_out};  // Bit_Extender bit_extender_3
  Adder #(.width(32)) adder_1 (
    .a({pc_add_1_out_2, pc_add_1_out_2_2}), .b(bit_extender_3_out), .out(adder_1_out));  // open: cin, cout
  Multiplexer #(.width(32)) multiplexer_1 (
    .in0({pc_add_1_out_2, pc_add_1_out_2_2}), .in1(adder_1_out), .out(multiplexer_1_out), .sel(PCSrc));  // open: en
  Multiplexer #(.width(32)) multiplexer_2 (
    .in0(multiplexer_1_out), .in1({pc_add_1_out_2, shifter_1_out}), .out(multiplexer_2_out), .sel(PCJump));  // open: en

  // Notes on the sheet:
  //   contents of rom_1 (hex, n*v repeats v):
  //   3631000b 36520005 02329821 00000000 0232a023 3c150008 ac130000 8c160004 8c130004 8c160004 1274fff7
endmodule

module EXT (
  input  [15:0] in_1,
  input  extsel,
  output [31:0] out_3
);

  wire [31:0] bit_extender_1_out, bit_extender_2_out;

  assign bit_extender_1_out = {{16{1'b0}}, in_1};  // Bit_Extender bit_extender_1
  assign bit_extender_2_out = {{16{in_1[15]}}, in_1};  // Bit_Extender bit_extender_2
  Multiplexer #(.width(32)) multiplexer_1 (
    .in0(bit_extender_1_out), .in1(bit_extender_2_out), .out(out_3), .sel(extsel));  // open: en
endmodule

module Controller (
  input  [5:0] op,
  input  [5:0] func,
  output RegDst,
  output RegWrite,
  output ALUSrc,
  output branch,
  output PCJump,
  output MemRead,
  output MemWrite,
  output MemtoReg,
  output extsel,
  output [3:0] ALU
);

  wire addu_out, beq_out, j_out, lui_out, lw_out, not_1_out, not_2_out, not_3_out, not_4_out, not_5_out,
       not_6_out, not_7_out, not_8_out, not_9_out, not_10_out, not_11_out, not_12_out, ori_out, subu_out,
       sw_out;

  not not_1 (not_1_out, op[5]);
  not not_2 (not_2_out, op[4]);
  not not_3 (not_3_out, op[2]);
  not not_4 (not_4_out, op[3]);
  not not_5 (not_5_out, func[5]);
  not not_6 (not_6_out, op[0]);
  not not_7 (not_7_out, op[1]);
  not not_8 (not_8_out, func[4]);
  not not_9 (not_9_out, func[3]);
  not not_10 (not_10_out, func[0]);
  not not_11 (not_11_out, func[1]);
  not not_12 (not_12_out, func[2]);
  and addu (addu_out, func[5], not_8_out, not_9_out, not_12_out, not_11_out, func[0], not_1_out, not_2_out, not_4_out, not_3_out, not_7_out, not_6_out);
  and subu (subu_out, func[5], not_8_out, not_9_out, not_12_out, func[1], func[0], not_1_out, not_2_out, not_4_out, not_3_out, not_7_out, not_6_out);
  and ori (ori_out, not_1_out, not_2_out, op[3], op[2], not_7_out, op[0]);
  and lw (lw_out, op[5], not_2_out, not_4_out, not_3_out, op[1], op[0]);
  and sw (sw_out, op[5], not_2_out, op[3], not_3_out, op[1], op[0]);
  and beq (beq_out, not_1_out, not_2_out, not_4_out, op[2], not_7_out, not_6_out);
  and lui (lui_out, not_1_out, not_2_out, op[3], op[2], op[1], op[0]);
  and j (j_out, not_1_out, not_2_out, not_4_out, not_3_out, op[1], not_6_out);
  or or_1 (RegDst, addu_out, subu_out);
  or or_2 (RegWrite, addu_out, subu_out, ori_out, lw_out, lui_out);
  or or_3 (ALUSrc, ori_out, lw_out, sw_out, lui_out);
  buf or_4 (branch, beq_out);  // OR_Gate
  buf or_5 (PCJump, j_out);  // OR_Gate
  buf or_6 (MemRead, lw_out);  // OR_Gate
  buf or_7 (MemWrite, sw_out);  // OR_Gate
  buf or_8 (MemtoReg, lw_out);  // OR_Gate
  or or_9 (extsel, lw_out, sw_out);
  or or_10 (ALU[0], subu_out, beq_out);
  buf or_11 (ALU[1], ori_out);  // OR_Gate
  buf or_12 (ALU[2], lui_out);  // OR_Gate
  buf or_13 (ALU[3], 1'b0);  // OR_Gate
endmodule

module sel26 (
  input  [31:0] in_1,
  output [4:0] out_2
);


  assign out_2 = in_1[6:2];
endmodule

module \and  (
  input  [31:0] in_1,
  input  [31:0] in_2,
  output [31:0] out_3
);

  assign out_3 = in_1 & in_2;  // AND_Gate and_1, 32 bits wide
endmodule
